# Fritzing sketch wiring (saved by Fritzing 0.9.3b)
circuit board: 8.46667cm x 5.64444cm
breadboards: 1

parts:
  VCC1 = Battery block 9V
  Arduino_Pro_Micro = Arduino Pro Mini (3.3V)
  Photodiode = PHOTOCELL [package=photocell]
  R2 = Resistor [tolerance=±5% resistance=10k package=THT]
  J1 = Basic Servo
  Stepper = Stepper Motor - Bipolar
  Stepper_Driver = IC, DIP package, 12 pins [chip_label="ZC-A0591 "]

nets:
  GND: VCC1.-, Arduino_Pro_Micro.GND, Arduino_Pro_Micro.A0, R2.Pin_0, J1.gnd, Stepper_Driver.pin6
  N1: VCC1.+, Arduino_Pro_Micro.RAW, Stepper_Driver.pin5
  VCC: Arduino_Pro_Micro.VCC, Photodiode.P$2, J1.vcc
  N2: Arduino_Pro_Micro.D10, J1.pulse
  N3: Arduino_Pro_Micro.D9, Stepper_Driver.pin1
  N4: Arduino_Pro_Micro.D8, Stepper_Driver.pin2
  N5: Arduino_Pro_Micro.D7, Stepper_Driver.pin3
  N6: Arduino_Pro_Micro.D6, Stepper_Driver.pin4
  N7: Photodiode.P$1, R2.Pin_1
  N8: Stepper.A, Stepper_Driver.pin10
  N9: Stepper.C, Stepper_Driver.pin9
  N10: Stepper.B, Stepper_Driver.pin8
  N11: Stepper.D, Stepper_Driver.pin7

notes:
  Arduino Pro Micro is used in the real Version - NOT the Pro Mini
  The Arduino Pro Mini is just a placeholder for the Pro Micro
